// Logisim project 64x8-ram.circ as structural Verilog: 1 circuit, main circuit main
module main (
  input  in_1,
  input  in_2,
  input  in_3,
  input  in_4,
  input  in_5,
  input  in_6,
  input  in_7,
  input  in_8,
  input  in_9,
  input  in_10,
  input  in_11,
  input  in_12,
  input  in_13,
  input  in_14,
  input  in_15,
  input  in_16
);

  wire clock_1_out, not_1_out, not_2_out;
  wire [7:0] ram_1_data;

  not not_1 (not_1_out, in_9);
  RAM #(.addrWidth(5)) ram_1 (
    .addr({in_10, in_11, in_12, in_13, in_14}), .data(ram_1_data), .sel(not_1_out), .clk(clock_1_out),
    .ld(not_2_out), .clr(in_16));
  RAM #(.addrWidth(5)) ram_2 (
    .addr({in_10, in_11, in_12, in_13, in_14}), .data(ram_1_data), .sel(in_9), .clk(clock_1_out),
    .ld(not_2_out), .clr(in_16));
  Clock clock_1 (.out(clock_1_out));
  // Probe on ram_1_data
  not not_2 (not_2_out, in_15);
  assign ram_1_data = in_15 ? {in_1, in_2, in_3, in_4, in_5, in_6, in_7, in_8} : 8'bz;  // Controlled_Buffer controlled_buffer_1

  // Notes on the sheet:
  //   1 memoria ram 64x8
  //   2 mermorias ram 32x8
  //   2 memorias ram 32x8
endmodule
