// Logisim project associação de 4 memorias rom em uma memoria 32x16.circ as structural Verilog: 1 circuit, main circuit main
module main (
  input  in_1,
  input  in_2,
  input  in_3,
  input  in_4,
  input  in_5
);

  wire not_1_out;
  wire [7:0] rom_1_data, rom_2_data;

  not not_1 (not_1_out, in_1);
  ROM #(.addrWidth(4)) rom_1 (.addr({in_2, in_3, in_4, in_5}), .data(rom_1_data), .sel(not_1_out));
  ROM #(.addrWidth(4)) rom_2 (.addr({in_2, in_3, in_4, in_5}), .data(rom_2_data), .sel(not_1_out));
  ROM #(.addrWidth(4)) rom_3 (.addr({in_2, in_3, in_4, in_5}), .data(rom_1_data), .sel(in_1));
  ROM #(.addrWidth(4)) rom_4 (.addr({in_2, in_3, in_4, in_5}), .data(rom_2_data), .sel(in_1));
  // Probe on {rom_1_data, rom_2_data}
endmodule
